# Fritzing sketch plantkit (saved by Fritzing 0.9.4)
breadboards: 1

parts:
  M1 = DOIT Esp32 DevKit v1 (30 pins long, 11 pins width) [part_number=ESP32S-PIN30]
  Part1 = Adafruit AHT20 Temperature and Humidity Sensor [part_number="Adafruit #4566"]
  Capacitive_Soil_Moisture_Sensor1 = DFRobot Capacitive Soil Moisture Sensor V1.0 [part_number=SEN0193]
  Capacitive_Soil_Moisture_Sensor2 = DFRobot Capacitive Soil Moisture Sensor V1.0 [part_number=SEN0193]

nets:
  VCC: M1.3V3, Part1.VCC, Capacitive_Soil_Moisture_Sensor1.VCC, Capacitive_Soil_Moisture_Sensor2.VCC
  GND: M1.GND, Part1.GND, Capacitive_Soil_Moisture_Sensor1.GND, Capacitive_Soil_Moisture_Sensor2.GND
  N1: M1.D21, Part1.SDA
  N2: M1.D22, Part1.SCL
  N3: M1.D34, Capacitive_Soil_Moisture_Sensor1.A
  N4: M1.D35, Capacitive_Soil_Moisture_Sensor2.A

custom parts:
  DOIT Esp32 DevKit v1 (30 pins long, 11 pins width): The DOIT Esp32 DevKit v1 is one of the development board created by DOIT to evaluate the ESP-WROOM-32 module. It is based on the ESP32 microcontroller that boasts Wifi, Bluetooth, Ethernet and Low Power support all in a single chip. (vanepp) made breadboard work, adjusted pin numbering and labels and reduced size of schematic and cleaned up pcb. This chip is 30pins long (2 x15) and 11 pins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
  Adafruit AHT20 Temperature and Humidity Sensor: The AHT20 is a nice but inexpensive temperature and humidity sensor from the same folks that brought us the DHT22. You can take sensor readings as often as you like, and it uses standard I2C so its super easy to use with any Arduino or Linux/Raspberry Pi board. This sensor has a typical accuracy of +- 2% relative humidity, and +-0.3 °C. There is only one I2C address so its not a good option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
  DFRobot Capacitive Soil Moisture Sensor V1.0: DFRobot Capacitive Soil Moisture Sensor V1.0 This product measures soil moisture levels by capacitive sensing, rather than resistive sensing like other types of moisture sensor. It is made of a corrosion resistant material giving it a long service life. Insert it into soil and impress your friends with the real-time soil moisture data! The product includes an on-board voltage regulator which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
